// Logisim project mux.circ as structural Verilog: 1 circuit, main circuit mux
module mux (
  input  a,
  input  s
);

  // AND_Gate and_1 has open pins: in0=a, out=open
  // AND_Gate and_2 is placed but not wired
  // OR_Gate or_1 is placed but not wired
endmodule
